// Logisim project SIngleCycle_CPULogisimNuevo.circ as structural Verilog: 20 circuits, main circuit main
module main (
  input  in_1,
  output [31:0] out_2
);

  wire alu_32bits_1_zero, and_1_out, CLK, ctrl_1_alusrc, ctrl_1_branch, ctrl_1_jump, ctrl_1_regwrite,
       Jump_register, JumpLink, MemRead, MemtoReg, MemWrite, RegDst;
  wire [1:0] ctrl_1_aluop;
  wire [2:0] aluctrl_1_aluoperation;
  wire [4:0] multiplexer_1_out, multiplexer_2_out;
  wire [5:0] Opcode;
  wire [23:0] register_1_q, shifter_1_out, shifter_3_out;
  wire [25:0] Address;
  wire [27:0] sl2_1_out_2;
  wire [31:0] adder_2_out, alu_32bits_1_out_4, extendsign_1_inmediate_extendido, multiplexer_3_out,
       multiplexer_4_out, multiplexer_5_out, multiplexer_7_out, Next_PC, PC, ram_2_dout, regfile_1_readdata1,
       regfile_1_readdata2, shifter_2_out;
  wire [31:24] register_1_q_2;

  // Probe on Next_PC
  Clock clock_1 (.out(CLK));
  Register #(.width(32)) register_1 (
    .D(Next_PC), .clk(CLK), .Q({register_1_q_2, register_1_q}), .clr(in_1));  // open: en
  // Probe on {register_1_q_2, register_1_q}
  Shifter #(.width(24), .shift("lr")) shifter_1 (.in(register_1_q), .\dist (5'b00010), .out(shifter_1_out));
  RAM #(.addrWidth(24), .dataWidth(32)) ram_1 (
    .addr(shifter_1_out), .we(1'b0), .oe(1'b1), .clk(CLK), .data({Opcode, Address}));
  // Probe on Address
  // Probe on Opcode
  // Probe on {Opcode, Address}
  SL2 sl2_1 (.Address(Address), .out_2(sl2_1_out_2));
  // Probe on sl2_1_out_2
  // Probe on PC[31:28]
  Adder #(.width(32)) adder_1 (.a({register_1_q_2, register_1_q}), .b(32'h4), .out(PC));  // open: cin, cout
  // Probe on PC
  // Probe on Address
  // Probe on Address[15:11]
  // Probe on Address[15:0]
  // Probe on {PC[31:28], sl2_1_out_2}
  // Probe on Address[25:21]
  Multiplexer #(.width(5), .enable("false")) multiplexer_1 (
    .in0(Address[20:16]), .in1(Address[15:11]), .out(multiplexer_1_out), .sel(RegDst));
  // Probe on shifter_2_out
  // Probe on Address[20:16]
  // Probe on multiplexer_2_out
  Multiplexer #(.width(5), .enable("false")) multiplexer_2 (
    .in0(multiplexer_1_out), .in1({5{1'b1}}), .out(multiplexer_2_out), .sel(JumpLink));
  Ctrl ctrl_1 (
    .OpCode(Opcode), .RegDst(RegDst), .Jump(ctrl_1_jump), .Branch(ctrl_1_branch), .MemRead(MemRead),
    .MemtoReg(MemtoReg), .ALUOp(ctrl_1_aluop), .MemWrite(MemWrite), .ALUSrc(ctrl_1_alusrc),
    .RegWrite(ctrl_1_regwrite), .JumpandLink(JumpLink));
  Adder #(.width(32)) adder_2 (.a(PC), .b(shifter_2_out), .out(adder_2_out));  // open: cin, cout
  Shifter #(.width(32)) shifter_2 (.in(extendsign_1_inmediate_extendido), .\dist (5'b00010), .out(shifter_2_out));
  // Probe on out_2
  // Probe on Address[5:0]
  // Probe on adder_2_out
  and and_1 (and_1_out, ctrl_1_branch, alu_32bits_1_zero);
  // Probe on regfile_1_readdata1
  RegFile regfile_1 (
    .RegWrite(ctrl_1_regwrite), .Read_Reg_1(Address[25:21]), .Read_Reg_2(Address[20:16]),
    .Write_Reg(multiplexer_2_out), .Write_Data(out_2), .CLK(CLK), .ReadData1(regfile_1_readdata1),
    .ReadData2(regfile_1_readdata2));  // open: Reset
  // Probe on regfile_1_readdata2
  // Probe on extendsign_1_inmediate_extendido
  Multiplexer #(.width(32), .enable("false")) multiplexer_3 (
    .in0(PC), .in1(adder_2_out), .out(multiplexer_3_out), .sel(and_1_out));
  // Probe on PC
  ExtendSign extendsign_1 (.Inmediate(Address[15:0]), .Inmediate_extendido(extendsign_1_inmediate_extendido));
  // Probe on multiplexer_4_out
  Multiplexer #(.width(32), .enable("false")) multiplexer_4 (
    .in0(multiplexer_3_out), .in1({PC[31:28], sl2_1_out_2}), .out(multiplexer_4_out), .sel(ctrl_1_jump));
  // Probe on regfile_1_readdata1
  // Probe on out_2
  Multiplexer #(.width(32), .enable("false")) multiplexer_5 (
    .in0(regfile_1_readdata2), .in1(extendsign_1_inmediate_extendido), .out(multiplexer_5_out),
    .sel(ctrl_1_alusrc));
  // Probe on Next_PC
  Multiplexer #(.width(32), .enable("false")) multiplexer_6 (
    .in0(multiplexer_4_out), .in1(out_2), .out(Next_PC), .sel(Jump_register));
  // Probe on regfile_1_readdata2
  // Probe on alu_32bits_1_out_4
  ALU_32bits alu_32bits_1 (
    .in_1(aluctrl_1_aluoperation), .A(regfile_1_readdata1), .B(multiplexer_5_out),
    .out_4(alu_32bits_1_out_4), .Zero(alu_32bits_1_zero));
  // Probe on multiplexer_5_out
  ALUCtrl aluctrl_1 (.ALUOp(ctrl_1_aluop), .Funct(Address[5:0]), .ALUOperation(aluctrl_1_aluoperation));
  // Probe on aluctrl_1_aluoperation
  JumpRegister jumpregister_1 (.OpCode(Opcode), .Funct(Address[5:0]), .JumpRegister(Jump_register));
  Shifter #(.width(24), .shift("lr")) shifter_3 (.in(alu_32bits_1_out_4[23:0]), .\dist (5'b00010), .out(shifter_3_out));
  // Probe on regfile_1_readdata2
  // Probe on shifter_3_out
  // Probe on alu_32bits_1_out_4
  RAM #(.addrWidth(24), .dataWidth(32), .databus("bibus")) ram_2 (
    .addr(shifter_3_out), .we(MemWrite), .oe(MemRead), .clk(CLK), .din(regfile_1_readdata2), .dout(ram_2_dout));
  // Probe on multiplexer_7_out
  Multiplexer #(.width(32), .enable("false")) multiplexer_7 (
    .in0(alu_32bits_1_out_4), .in1(ram_2_dout), .out(multiplexer_7_out), .sel(MemtoReg));
  // Probe on ram_2_dout
  Multiplexer #(.width(32), .enable("false")) multiplexer_8 (
    .in0(multiplexer_7_out), .in1(PC), .out(out_2), .sel(JumpLink));
  // Probe on PC

  // Other names for the same wires on the sheet: Write_Data[31:0] = out_2
endmodule

module RegFile (
  input  RegWrite,
  input  [4:0] Read_Reg_1,
  input  [4:0] Read_Reg_2,
  input  [4:0] Write_Reg,
  input  [31:0] Write_Data,
  input  CLK,
  input  Reset,
  output [31:0] ReadData1,
  output [31:0] ReadData2
);

  wire Reg0Enable, Reg1Enable, Reg2Enable, Reg3Enable, Reg4Enable, Reg5Enable, Reg6Enable, Reg7Enable,
       Reg8Enable, Reg9Enable, Reg10Enable, Reg11Enable, Reg12Enable, Reg13Enable, Reg14Enable, Reg15Enable,
       Reg16Enable, Reg17Enable, Reg18Enable, Reg19Enable, Reg20Enable, Reg21Enable, Reg22Enable,
       Reg23Enable, Reg24Enable, Reg25Enable, Reg26Enable, Reg27Enable, Reg28Enable, Reg29Enable,
       Reg30Enable, Reg31Enable;
  wire [31:0] Reg0, Reg1, Reg2, Reg3, Reg4, Reg5, Reg6, Reg7, Reg8, Reg9, Reg10, Reg11, Reg12, Reg13, Reg14,
       Reg15, Reg16, Reg17, Reg18, Reg19, Reg20, Reg21, Reg22, Reg23, Reg24, Reg25, Reg26, Reg27, Reg28,
       Reg29, Reg30, Reg31;

  // Probe on Read_Reg_2
  // Probe on Write_Reg
  // Probe on Write_Data
  RegFileEnable regfileenable_1 (
    .WriteReg(Write_Reg), .RegWrite(RegWrite), .WriteEnable0(Reg0Enable), .WriteEnable1(Reg1Enable),
    .WriteEnable2(Reg2Enable), .WriteEnable3(Reg3Enable), .WriteEnable4(Reg4Enable),
    .WriteEnable5(Reg5Enable), .WriteEnable6(Reg6Enable), .WriteEnable7(Reg7Enable),
    .WriteEnable8(Reg8Enable), .WriteEnable9(Reg9Enable), .WriteEnable10(Reg10Enable),
    .WriteEnable11(Reg11Enable), .WriteEnable12(Reg12Enable), .WriteEnable13(Reg13Enable),
    .WriteEnable14(Reg14Enable), .WriteEnable15(Reg15Enable), .WriteEnable16(Reg16Enable),
    .WriteEnable17(Reg17Enable), .WriteEnable18(Reg18Enable), .WriteEnable19(Reg19Enable),
    .WriteEnable20(Reg20Enable), .WriteEnable21(Reg21Enable), .WriteEnable22(Reg22Enable),
    .WriteEnable23(Reg23Enable), .WriteEnable24(Reg24Enable), .WriteEnable25(Reg25Enable),
    .WriteEnable26(Reg26Enable), .WriteEnable27(Reg27Enable), .WriteEnable28(Reg28Enable),
    .WriteEnable29(Reg29Enable), .WriteEnable30(Reg30Enable), .WriteEnable31(Reg31Enable));
  Register #(.width(32)) u_Reg0 (.D(Write_Data), .en(1'b0), .clk(CLK), .Q(Reg0));  // open: clr
  Register #(.width(32)) u_Reg1 (.D(Write_Data), .en(Reg1Enable), .clk(CLK), .Q(Reg1));  // open: clr
  Register #(.width(32)) u_Reg2 (.D(Write_Data), .en(Reg2Enable), .clk(CLK), .Q(Reg2));  // open: clr
  Register #(.width(32)) u_Reg3 (.D(Write_Data), .en(Reg3Enable), .clk(CLK), .Q(Reg3));  // open: clr
  Register #(.width(32)) u_Reg4 (.D(Write_Data), .en(Reg4Enable), .clk(CLK), .Q(Reg4));  // open: clr
  Register #(.width(32)) u_Reg5 (.D(Write_Data), .en(Reg5Enable), .clk(CLK), .Q(Reg5));  // open: clr
  Register #(.width(32)) u_Reg6 (.D(Write_Data), .en(Reg6Enable), .clk(CLK), .Q(Reg6));  // open: clr
  Register #(.width(32)) u_Reg7 (.D(Write_Data), .en(Reg7Enable), .clk(CLK), .Q(Reg7));  // open: clr
  Register #(.width(32)) u_Reg8 (.D(Write_Data), .en(Reg8Enable), .clk(CLK), .Q(Reg8));  // open: clr
  Register #(.width(32)) u_Reg9 (.D(Write_Data), .en(Reg9Enable), .clk(CLK), .Q(Reg9));  // open: clr
  Register #(.width(32)) u_Reg10 (.D(Write_Data), .en(Reg10Enable), .clk(CLK), .Q(Reg10));  // open: clr
  Register #(.width(32)) u_Reg11 (.D(Write_Data), .en(Reg11Enable), .clk(CLK), .Q(Reg11));  // open: clr
  Register #(.width(32)) u_Reg12 (.D(Write_Data), .en(Reg12Enable), .clk(CLK), .Q(Reg12));  // open: clr
  Register #(.width(32)) u_Reg13 (.D(Write_Data), .en(Reg13Enable), .clk(CLK), .Q(Reg13));  // open: clr
  Register #(.width(32)) u_Reg14 (.D(Write_Data), .en(Reg14Enable), .clk(CLK), .Q(Reg14));  // open: clr
  Register #(.width(32)) u_Reg15 (.D(Write_Data), .en(Reg15Enable), .clk(CLK), .Q(Reg15));  // open: clr
  Register #(.width(32)) register_1 (.D(Write_Data), .en(Reg16Enable), .clk(CLK), .Q(Reg16));  // open: clr
  Register #(.width(32)) register_2 (.D(Write_Data), .en(Reg17Enable), .clk(CLK), .Q(Reg17));  // open: clr
  Register #(.width(32)) register_3 (.D(Write_Data), .en(Reg18Enable), .clk(CLK), .Q(Reg18));  // open: clr
  Register #(.width(32)) register_4 (.D(Write_Data), .en(Reg19Enable), .clk(CLK), .Q(Reg19));  // open: clr
  Register #(.width(32)) register_5 (.D(Write_Data), .en(Reg20Enable), .clk(CLK), .Q(Reg20));  // open: clr
  Register #(.width(32)) register_6 (.D(Write_Data), .en(Reg21Enable), .clk(CLK), .Q(Reg21));  // open: clr
  Register #(.width(32)) register_7 (.D(Write_Data), .en(Reg22Enable), .clk(CLK), .Q(Reg22));  // open: clr
  Register #(.width(32)) register_8 (.D(Write_Data), .en(Reg23Enable), .clk(CLK), .Q(Reg23));  // open: clr
  Register #(.width(32)) register_9 (.D(Write_Data), .en(Reg24Enable), .clk(CLK), .Q(Reg24));  // open: clr
  Register #(.width(32)) register_10 (.D(Write_Data), .en(Reg25Enable), .clk(CLK), .Q(Reg25));  // open: clr
  Register #(.width(32)) register_11 (.D(Write_Data), .en(Reg26Enable), .clk(CLK), .Q(Reg26));  // open: clr
  Register #(.width(32)) register_12 (.D(Write_Data), .en(Reg27Enable), .clk(CLK), .Q(Reg27));  // open: clr
  Register #(.width(32)) register_13 (.D(Write_Data), .en(Reg28Enable), .clk(CLK), .Q(Reg28));  // open: clr
  Register #(.width(32)) register_14 (.D(Write_Data), .en(Reg30Enable), .clk(CLK), .Q(Reg30));  // open: clr
  Register #(.width(32)) register_15 (.D(Write_Data), .en(Reg31Enable), .clk(CLK), .Q(Reg31));  // open: clr
  Register #(.width(32)) register_16 (.D(Write_Data), .en(Reg29Enable), .clk(CLK), .Q(Reg29));  // open: clr
  RegFileRead regfileread_1 (
    .Read_Reg_1(Read_Reg_1), .Read_Reg_2(Read_Reg_2), .Reg0(Reg0), .Reg1(Reg1), .Reg2(Reg2), .Reg3(Reg3),
    .Reg4(Reg4), .Reg5(Reg5), .Reg6(Reg6), .Reg7(Reg7), .Reg8(Reg8), .Reg9(Reg9), .Reg10(Reg10),
    .Reg11(Reg11), .Reg12(Reg12), .Reg13(Reg13), .Reg14(Reg14), .Reg15(Reg15), .Reg16(Reg16), .Reg17(Reg17),
    .Reg18(Reg18), .Reg19(Reg19), .Reg20(Reg20), .Reg21(Reg21), .Reg22(Reg22), .Reg23(Reg23), .Reg24(Reg24),
    .Reg25(Reg25), .Reg26(Reg26), .Reg27(Reg27), .Reg28(Reg28), .Reg29(Reg29), .Reg30(Reg30), .Reg31(Reg31),
    .out_35(ReadData1), .out_36(ReadData2));

  // Other names for the same wires on the sheet: Clock = CLK; WriteData[31:0] = Write_Data
endmodule

module RegFileEnable (
  input  [4:0] WriteReg,
  input  RegWrite,
  output WriteEnable0,
  output WriteEnable1,
  output WriteEnable2,
  output WriteEnable3,
  output WriteEnable4,
  output WriteEnable5,
  output WriteEnable6,
  output WriteEnable7,
  output WriteEnable8,
  output WriteEnable9,
  output WriteEnable10,
  output WriteEnable11,
  output WriteEnable12,
  output WriteEnable13,
  output WriteEnable14,
  output WriteEnable15,
  output WriteEnable16,
  output WriteEnable17,
  output WriteEnable18,
  output WriteEnable19,
  output WriteEnable20,
  output WriteEnable21,
  output WriteEnable22,
  output WriteEnable23,
  output WriteEnable24,
  output WriteEnable25,
  output WriteEnable26,
  output WriteEnable27,
  output WriteEnable28,
  output WriteEnable29,
  output WriteEnable30,
  output WriteEnable31
);

  wire Reg0Enable, Reg1Enable, Reg2Enable, Reg3Enable, Reg4Enable, Reg5Enable, Reg6Enable, Reg7Enable,
       Reg8Enable, Reg9Enable, Reg10Enable, Reg11Enable, Reg12Enable, Reg13Enable, Reg14Enable, Reg15Enable,
       Reg16Enable, Reg17Enable, Reg18Enable, Reg19Enable, Reg20Enable, Reg21Enable, Reg22Enable,
       Reg23Enable, Reg24Enable, Reg25Enable, Reg26Enable, Reg27Enable, Reg28Enable, Reg29Enable,
       Reg30Enable, Reg31Enable;

  // Probe on WriteReg
  Decoder #(.select(5), .enable("false")) decoder_1 (
    .out0(Reg0Enable), .out1(Reg1Enable), .out2(Reg2Enable), .out3(Reg3Enable), .out4(Reg4Enable),
    .out5(Reg5Enable), .out6(Reg6Enable), .out7(Reg7Enable), .out8(Reg8Enable), .out9(Reg9Enable),
    .out10(Reg10Enable), .out11(Reg11Enable), .out12(Reg12Enable), .out13(Reg13Enable), .out14(Reg14Enable),
    .out15(Reg15Enable), .out16(Reg16Enable), .out17(Reg17Enable), .out18(Reg18Enable), .out19(Reg19Enable),
    .out20(Reg20Enable), .out21(Reg21Enable), .out22(Reg22Enable), .out23(Reg23Enable), .out24(Reg24Enable),
    .out25(Reg25Enable), .out26(Reg26Enable), .out27(Reg27Enable), .out28(Reg28Enable), .out29(Reg29Enable),
    .out30(Reg30Enable), .out31(Reg31Enable), .sel(WriteReg));
  and and_1 (WriteEnable0, Reg0Enable, RegWrite);
  and and_2 (WriteEnable1, Reg1Enable, RegWrite);
  and and_3 (WriteEnable2, Reg2Enable, RegWrite);
  and and_4 (WriteEnable3, Reg3Enable, RegWrite);
  and and_5 (WriteEnable4, Reg4Enable, RegWrite);
  and and_6 (WriteEnable5, Reg5Enable, RegWrite);
  and and_7 (WriteEnable6, Reg6Enable, RegWrite);
  and and_8 (WriteEnable7, Reg7Enable, RegWrite);
  and and_9 (WriteEnable8, Reg8Enable, RegWrite);
  and and_10 (WriteEnable9, Reg9Enable, RegWrite);
  and and_11 (WriteEnable10, Reg10Enable, RegWrite);
  and and_12 (WriteEnable11, Reg11Enable, RegWrite);
  and and_13 (WriteEnable12, Reg12Enable, RegWrite);
  and and_14 (WriteEnable13, Reg13Enable, RegWrite);
  and and_15 (WriteEnable14, Reg14Enable, RegWrite);
  and and_16 (WriteEnable15, Reg15Enable, RegWrite);
  and and_17 (WriteEnable16, Reg16Enable, RegWrite);
  and and_18 (WriteEnable17, Reg17Enable, RegWrite);
  and and_19 (WriteEnable18, Reg18Enable, RegWrite);
  and and_20 (WriteEnable19, Reg19Enable, RegWrite);
  and and_21 (WriteEnable20, Reg20Enable, RegWrite);
  and and_22 (WriteEnable21, Reg21Enable, RegWrite);
  and and_23 (WriteEnable22, Reg22Enable, RegWrite);
  and and_24 (WriteEnable23, Reg23Enable, RegWrite);
  and and_25 (WriteEnable24, Reg24Enable, RegWrite);
  and and_26 (WriteEnable25, Reg25Enable, RegWrite);
  and and_27 (WriteEnable26, Reg26Enable, RegWrite);
  and and_28 (WriteEnable27, Reg27Enable, RegWrite);
  and and_29 (WriteEnable28, Reg28Enable, RegWrite);
  and and_30 (WriteEnable29, Reg29Enable, RegWrite);
  and and_31 (WriteEnable30, Reg30Enable, RegWrite);
  and and_32 (WriteEnable31, Reg31Enable, RegWrite);
endmodule

module RegFileRead (
  input  [4:0] Read_Reg_1,
  input  [4:0] Read_Reg_2,
  input  [31:0] Reg0,
  input  [31:0] Reg1,
  input  [31:0] Reg2,
  input  [31:0] Reg3,
  input  [31:0] Reg4,
  input  [31:0] Reg5,
  input  [31:0] Reg6,
  input  [31:0] Reg7,
  input  [31:0] Reg8,
  input  [31:0] Reg9,
  input  [31:0] Reg10,
  input  [31:0] Reg11,
  input  [31:0] Reg12,
  input  [31:0] Reg13,
  input  [31:0] Reg14,
  input  [31:0] Reg15,
  input  [31:0] Reg16,
  input  [31:0] Reg17,
  input  [31:0] Reg18,
  input  [31:0] Reg19,
  input  [31:0] Reg20,
  input  [31:0] Reg21,
  input  [31:0] Reg22,
  input  [31:0] Reg23,
  input  [31:0] Reg24,
  input  [31:0] Reg25,
  input  [31:0] Reg26,
  input  [31:0] Reg27,
  input  [31:0] Reg28,
  input  [31:0] Reg29,
  input  [31:0] Reg30,
  input  [31:0] Reg31,
  output [31:0] out_35,
  output [31:0] out_36
);

  Multiplexer #(.select(5), .width(32)) multiplexer_1 (
    .in0(Reg0), .in1(Reg1), .in2(Reg2), .in3(Reg3), .in4(Reg4), .in5(Reg5), .in6(Reg6), .in7(Reg7),
    .in8(Reg8), .in9(Reg9), .in10(Reg10), .in11(Reg11), .in12(Reg12), .in13(Reg13), .in14(Reg14),
    .in15(Reg15), .in16(Reg16), .in17(Reg17), .in18(Reg18), .in19(Reg19), .in20(Reg20), .in21(Reg21),
    .in22(Reg22), .in23(Reg23), .in24(Reg24), .in25(Reg25), .in26(Reg26), .in27(Reg27), .in28(Reg28),
    .in29(Reg29), .in30(Reg30), .in31(Reg31), .out(out_35), .sel(Read_Reg_1));  // open: en
  Multiplexer #(.select(5), .width(32)) multiplexer_2 (
    .in0(Reg0), .in1(Reg1), .in2(Reg2), .in3(Reg3), .in4(Reg4), .in5(Reg5), .in6(Reg6), .in7(Reg7),
    .in8(Reg8), .in9(Reg9), .in10(Reg10), .in11(Reg11), .in12(Reg12), .in13(Reg13), .in14(Reg14),
    .in15(Reg15), .in16(Reg16), .in17(Reg17), .in18(Reg18), .in19(Reg19), .in20(Reg20), .in21(Reg21),
    .in22(Reg22), .in23(Reg23), .in24(Reg24), .in25(Reg25), .in26(Reg26), .in27(Reg27), .in28(Reg28),
    .in29(Reg29), .in30(Reg30), .in31(Reg31), .out(out_36), .sel(Read_Reg_2));  // open: en
  // Probe on nothing
endmodule

module Sumador1bit (
  input  Cin,
  input  A,
  input  B,
  output S,
  output Cout
);

  wire and_1_out, and_2_out, and_3_out, and_4_out, and_5_out, and_6_out, and_7_out, not_1_out, not_2_out,
       not_3_out, not_4_out, not_5_out, not_6_out;

  not not_1 (not_1_out, Cin);
  not not_2 (not_2_out, A);
  not not_3 (not_3_out, Cin);
  not not_4 (not_4_out, B);
  not not_5 (not_5_out, A);
  not not_6 (not_6_out, B);
  and and_1 (and_1_out, A, B);
  and and_2 (and_2_out, Cin, B);
  and and_3 (and_3_out, Cin, A);
  and and_4 (and_4_out, not_1_out, not_2_out, B);
  and and_5 (and_5_out, not_3_out, A, not_4_out);
  and and_6 (and_6_out, Cin, not_5_out, not_6_out);
  and and_7 (and_7_out, Cin, A, B);
  or or_1 (Cout, and_1_out, and_2_out, and_3_out);
  or or_2 (S, and_4_out, and_5_out, and_6_out, and_7_out);
endmodule

module ALU_1bit (
  input  A,
  input  B,
  input  Binv,
  input  Cin,
  input  [2:0] ALU_op,
  input  STL,
  output Cout,
  output Salida
);

  wire AND, multiplexer_1_out, NOR, not_2_out, OR, Suma_resta_e7fbe0ac;

  and and_1 (AND, A, B);
  or or_1 (OR, A, B);
  not not_1 (NOR, OR);
  Multiplexer #(.enable("false")) multiplexer_1 (.in0(B), .in1(not_2_out), .out(multiplexer_1_out), .sel(Binv));
  not not_2 (not_2_out, B);
  Sumador1bit sumador1bit_1 (.Cin(Cin), .A(A), .B(multiplexer_1_out), .S(Suma_resta_e7fbe0ac), .Cout(Cout));
  Multiplexer #(.select(3), .enable("false")) multiplexer_2 (
    .in1(Suma_resta_e7fbe0ac), .in2(OR), .in3(Suma_resta_e7fbe0ac), .in4(NOR), .in5(AND), .in7(STL),
    .out(Salida), .sel(ALU_op));  // open: in0, in6

  // Other names for the same wires on the sheet: SLT = STL
endmodule

module Signo (
  input  Cout,
  input  Cin,
  output Overflow
);

  wire and_1_out, and_2_out, not_1_out, not_2_out;

  not not_1 (not_1_out, Cout);
  not not_2 (not_2_out, Cin);
  and and_1 (and_1_out, not_1_out, Cin);
  and and_2 (and_2_out, not_2_out, Cout);
  or or_1 (Overflow, and_1_out, and_2_out);
endmodule

module ALU_32bits (
  input  [2:0] in_1,
  input  [31:0] A,
  input  [31:0] B,
  output [31:0] out_4,
  output Zero
);

  wire binv, C0, C1, C2, C3, C4, C5, C6, C7, C8, C9, C10, C11, C12, C13, C14, C15, C16, C17, C18, C19, C20,
       C21, C22, C23, C24, C25, C26, C27, C28, C29, C30, C31, C32, SLT;

  Binv_cin binv_cin_1 (.ALUop2(in_1[2]), .Binv(binv), .ALUop1(in_1[1]), .ALUop0(in_1[0]), .Cin(C0));
  ALU_1bit_overflow alu_1bit_overflow_1 (
    .Salida(out_4[31]), .A(A[31]), .B(B[31]), .Cin(C31), .ALU_op(in_1), .Binv(binv), .Cout(C32), .STL(1'b0),
    .Sign(SLT));
  ALU_1bit alu_1bit_1 (
    .A(A[0]), .B(B[0]), .Cout(C1), .Salida(out_4[0]), .Cin(C0), .Binv(binv), .ALU_op(in_1), .STL(SLT));
  and and_1 (Zero, ~out_4[31], ~out_4[30], ~out_4[29], ~out_4[28], ~out_4[27], ~out_4[26], ~out_4[25], ~out_4[24], ~out_4[23], ~out_4[22], ~out_4[21], ~out_4[20], ~out_4[19], ~out_4[18], ~out_4[17], ~out_4[16], ~out_4[15], ~out_4[14], ~out_4[13], ~out_4[12], ~out_4[11], ~out_4[10], ~out_4[9], ~out_4[8], ~out_4[7], ~out_4[6], ~out_4[5], ~out_4[4], ~out_4[3], ~out_4[2], ~out_4[1], ~out_4[0]);  // AND_Gate
  ALU_1bit alu_1bit_2 (
    .A(A[30]), .B(B[30]), .Cout(C31), .Salida(out_4[30]), .Cin(C30), .Binv(binv), .ALU_op(in_1), .STL(1'b0));
  ALU_1bit alu_1bit_3 (
    .A(A[29]), .B(B[29]), .Cout(C30), .Salida(out_4[29]), .Cin(C29), .Binv(binv), .ALU_op(in_1), .STL(1'b0));
  ALU_1bit alu_1bit_4 (
    .A(A[28]), .B(B[28]), .Cout(C29), .Salida(out_4[28]), .Cin(C28), .Binv(binv), .ALU_op(in_1), .STL(1'b0));
  ALU_1bit alu_1bit_5 (
    .A(A[27]), .B(B[27]), .Cout(C28), .Salida(out_4[27]), .Cin(C27), .Binv(binv), .ALU_op(in_1), .STL(1'b0));
  ALU_1bit alu_1bit_6 (
    .A(A[26]), .B(B[26]), .Cout(C27), .Salida(out_4[26]), .Cin(C26), .Binv(binv), .ALU_op(in_1), .STL(1'b0));
  ALU_1bit alu_1bit_7 (
    .A(A[25]), .B(B[25]), .Cout(C26), .Salida(out_4[25]), .Cin(C25), .Binv(binv), .ALU_op(in_1), .STL(1'b0));
  ALU_1bit alu_1bit_8 (
    .A(A[24]), .B(B[24]), .Cout(C25), .Salida(out_4[24]), .Cin(C24), .Binv(binv), .ALU_op(in_1), .STL(1'b0));
  ALU_1bit alu_1bit_9 (
    .A(A[23]), .B(B[23]), .Cout(C24), .Salida(out_4[23]), .Cin(C23), .Binv(binv), .ALU_op(in_1), .STL(1'b0));
  ALU_1bit alu_1bit_10 (
    .A(A[22]), .B(B[22]), .Cout(C23), .Salida(out_4[22]), .Cin(C22), .Binv(binv), .ALU_op(in_1), .STL(1'b0));
  ALU_1bit alu_1bit_11 (
    .A(A[21]), .B(B[21]), .Cout(C22), .Salida(out_4[21]), .Cin(C21), .Binv(binv), .ALU_op(in_1), .STL(1'b0));
  ALU_1bit alu_1bit_12 (
    .A(A[20]), .B(B[20]), .Cout(C21), .Salida(out_4[20]), .Cin(C20), .Binv(binv), .ALU_op(in_1), .STL(1'b0));
  ALU_1bit alu_1bit_13 (
    .A(A[19]), .B(B[19]), .Cout(C20), .Salida(out_4[19]), .Cin(C19), .Binv(binv), .ALU_op(in_1), .STL(1'b0));
  ALU_1bit alu_1bit_14 (
    .A(A[18]), .B(B[18]), .Cout(C19), .Salida(out_4[18]), .Cin(C18), .Binv(binv), .ALU_op(in_1), .STL(1'b0));
  ALU_1bit alu_1bit_15 (
    .A(A[17]), .B(B[17]), .Cout(C18), .Salida(out_4[17]), .Cin(C17), .Binv(binv), .ALU_op(in_1), .STL(1'b0));
  ALU_1bit alu_1bit_16 (
    .A(A[16]), .B(B[16]), .Cout(C17), .Salida(out_4[16]), .Cin(C16), .Binv(binv), .ALU_op(in_1), .STL(1'b0));
  ALU_1bit alu_1bit_17 (
    .A(A[15]), .B(B[15]), .Cout(C16), .Salida(out_4[15]), .Cin(C15), .Binv(binv), .ALU_op(in_1), .STL(1'b0));
  ALU_1bit alu_1bit_18 (
    .A(A[14]), .B(B[14]), .Cout(C15), .Salida(out_4[14]), .Cin(C14), .Binv(binv), .ALU_op(in_1), .STL(1'b0));
  ALU_1bit alu_1bit_19 (
    .A(A[13]), .B(B[13]), .Cout(C14), .Salida(out_4[13]), .Cin(C13), .Binv(binv), .ALU_op(in_1), .STL(1'b0));
  ALU_1bit alu_1bit_20 (
    .A(A[12]), .B(B[12]), .Cout(C13), .Salida(out_4[12]), .Cin(C12), .Binv(binv), .ALU_op(in_1), .STL(1'b0));
  ALU_1bit alu_1bit_21 (
    .A(A[11]), .B(B[11]), .Cout(C12), .Salida(out_4[11]), .Cin(C11), .Binv(binv), .ALU_op(in_1), .STL(1'b0));
  ALU_1bit alu_1bit_22 (
    .A(A[10]), .B(B[10]), .Cout(C11), .Salida(out_4[10]), .Cin(C10), .Binv(binv), .ALU_op(in_1), .STL(1'b0));
  ALU_1bit alu_1bit_23 (
    .A(A[9]), .B(B[9]), .Cout(C10), .Salida(out_4[9]), .Cin(C9), .Binv(binv), .ALU_op(in_1), .STL(1'b0));
  ALU_1bit alu_1bit_24 (
    .A(A[8]), .B(B[8]), .Cout(C9), .Salida(out_4[8]), .Cin(C8), .Binv(binv), .ALU_op(in_1), .STL(1'b0));
  ALU_1bit alu_1bit_25 (
    .A(A[7]), .B(B[7]), .Cout(C8), .Salida(out_4[7]), .Cin(C7), .Binv(binv), .ALU_op(in_1), .STL(1'b0));
  ALU_1bit alu_1bit_26 (
    .A(A[6]), .B(B[6]), .Cout(C7), .Salida(out_4[6]), .Cin(C6), .Binv(binv), .ALU_op(in_1), .STL(1'b0));
  ALU_1bit alu_1bit_27 (
    .A(A[5]), .B(B[5]), .Cout(C6), .Salida(out_4[5]), .Cin(C5), .Binv(binv), .ALU_op(in_1), .STL(1'b0));
  ALU_1bit alu_1bit_28 (
    .A(A[4]), .B(B[4]), .Cout(C5), .Salida(out_4[4]), .Cin(C4), .Binv(binv), .ALU_op(in_1), .STL(1'b0));
  ALU_1bit alu_1bit_29 (
    .A(A[3]), .B(B[3]), .Cout(C4), .Salida(out_4[3]), .Cin(C3), .Binv(binv), .ALU_op(in_1), .STL(1'b0));
  ALU_1bit alu_1bit_30 (
    .A(A[2]), .B(B[2]), .Cout(C3), .Salida(out_4[2]), .Cin(C2), .Binv(binv), .ALU_op(in_1), .STL(1'b0));
  ALU_1bit alu_1bit_31 (
    .A(A[1]), .B(B[1]), .Cout(C2), .Salida(out_4[1]), .Cin(C1), .Binv(binv), .ALU_op(in_1), .STL(1'b0));

  // Other names for the same wires on the sheet: ALU_op[2:0] = in_1; R0 = out_4[0]; R1 = out_4[1]; R2 = out_4[2];
  //   R3 = out_4[3]; R4 = out_4[4]; R5 = out_4[5]; R6 = out_4[6]; R7 = out_4[7]; R8 = out_4[8]; R9 = out_4[9];
  //   R10 = out_4[10]; R11 = out_4[11]; R12 = out_4[12]; R13 = out_4[13]; R14 = out_4[14]; R15 = out_4[15];
  //   R16 = out_4[16]; R17 = out_4[17]; R18 = out_4[18]; R19 = out_4[19]; R20 = out_4[20]; R21 = out_4[21];
  //   R22 = out_4[22]; R23 = out_4[23]; R24 = out_4[24]; R25 = out_4[25]; R26 = out_4[26]; R27 = out_4[27];
  //   R28 = out_4[28]; R29 = out_4[29]; R30 = out_4[30]; R31 = out_4[31]
endmodule

module Binv_cin (
  input  ALUop2,
  input  ALUop1,
  input  ALUop0,
  output Binv,
  output Cin
);

  wire and_1_out, and_2_out, and_3_out, and_4_out, not_1_out, not_2_out, not_3_out, not_4_out;

  not not_1 (not_1_out, ALUop2);
  not not_2 (not_2_out, ALUop1);
  not not_3 (not_3_out, ALUop2);
  not not_4 (not_4_out, ALUop1);
  and and_1 (and_1_out, not_1_out, not_2_out, ALUop0);
  and and_2 (and_2_out, ALUop2, ALUop1, ALUop0);
  and and_3 (and_3_out, not_3_out, not_4_out, ALUop0);
  and and_4 (and_4_out, ALUop2, ALUop1, ALUop0);
  or or_1 (Binv, and_1_out, and_2_out);
  or or_2 (Cin, and_3_out, and_4_out);
endmodule

module ALU_1bit_overflow (
  input  A,
  input  B,
  input  [2:0] ALU_op,
  input  Binv,
  input  Cin,
  input  STL,
  output Salida,
  output Cout,
  output Sign
);

  wire AND, multiplexer_1_out, NOR, not_2_out, OR, signo_1_overflow, Suma_resta_e7fbe0ac;

  and and_1 (AND, A, B);
  or or_1 (OR, A, B);
  not not_1 (NOR, OR);
  Multiplexer #(.enable("false")) multiplexer_1 (.in0(B), .in1(not_2_out), .out(multiplexer_1_out), .sel(Binv));
  not not_2 (not_2_out, B);
  Sumador1bit sumador1bit_1 (.Cin(Cin), .A(A), .B(multiplexer_1_out), .S(Suma_resta_e7fbe0ac), .Cout(Cout));
  Signo signo_1 (.Cout(Cout), .Cin(Cin), .Overflow(signo_1_overflow));
  Multiplexer #(.select(3), .enable("false")) multiplexer_2 (
    .in1(Suma_resta_e7fbe0ac), .in2(OR), .in3(Suma_resta_e7fbe0ac), .in4(NOR), .in5(AND), .in7(STL),
    .out(Salida), .sel(ALU_op));  // open: in0, in6
  Multiplexer multiplexer_3 (.in0(Suma_resta_e7fbe0ac), .in1(Cout), .out(Sign), .sel(signo_1_overflow));  // open: en

  // Other names for the same wires on the sheet: SLT = STL
endmodule

module Ctrl (
  input  [5:0] OpCode,
  output RegDst,
  output Jump,
  output Branch,
  output MemRead,
  output MemtoReg,
  output [1:0] ALUOp,
  output MemWrite,
  output ALUSrc,
  output RegWrite,
  output JumpandLink
);

  wire and_4_out, and_5_out, not_2_out, not_3_out, not_4_out, not_5_out, not_6_out, not_7_out, not_8_out,
       not_9_out;

  not not_1 (RegDst, OpCode[1]);
  not not_2 (not_2_out, OpCode[5]);
  not not_3 (not_3_out, OpCode[3]);
  not not_4 (not_4_out, OpCode[2]);
  not not_5 (not_5_out, OpCode[1]);
  not not_6 (not_6_out, OpCode[2]);
  not not_7 (not_7_out, OpCode[1]);
  not not_8 (not_8_out, OpCode[3]);
  not not_9 (not_9_out, OpCode[5]);
  and and_1 (Jump, not_2_out, OpCode[1]);
  and and_2 (MemRead, OpCode[5], not_3_out);
  and and_3 (ALUOp[1], not_4_out, not_5_out);
  and and_4 (and_4_out, not_6_out, not_7_out);
  and and_5 (and_5_out, not_8_out, OpCode[0]);
  and and_6 (JumpandLink, not_9_out, OpCode[0]);
  or or_1 (RegWrite, and_4_out, and_5_out);

  assign ALUOp[0] = OpCode[2];
  assign ALUSrc = OpCode[1];
  assign Branch = OpCode[2];
  assign MemtoReg = OpCode[1];
  assign MemWrite = OpCode[3];
endmodule

module ExtendSign (
  input  [15:0] Inmediate,
  output [31:0] Inmediate_extendido
);


  assign Inmediate_extendido = {{17{Inmediate[15]}}, Inmediate[14:0]};
endmodule

module SL2 (
  input  [25:0] Address,
  output [27:0] out_2
);


  assign out_2 = {Address, 2'b00};
endmodule

module JumpRegister (
  input  [5:0] OpCode,
  input  [5:0] Funct,
  output JumpRegister
);

  wire and_1_out, and_2_out, not_2_out, not_3_out;
  wire [5:0] not_1_out;

  assign not_1_out = ~OpCode;  // NOT_Gate not_1, 6 bits wide
  not not_2 (not_2_out, Funct[5]);
  not not_3 (not_3_out, Funct[4]);
  and and_1 (and_1_out, not_2_out, not_3_out);
  and and_2 (and_2_out, not_1_out[5], not_1_out[4], not_1_out[3], not_1_out[2], not_1_out[1], not_1_out[0]);
  and and_3 (JumpRegister, and_2_out, and_1_out);
endmodule

module DataMemory (
  input  Mem_write,
  input  [31:0] Address,
  input  Mem_Read,
  input  CLK,
  input  [31:0] Write_Data,
  output [31:0] Read_Data
);

  wire [23:0] shifter_1_out;

  Shifter #(.width(24), .shift("lr")) shifter_1 (.in(Address[23:0]), .\dist (5'b00010), .out(shifter_1_out));
  RAM #(.addrWidth(24), .dataWidth(32)) ram_1 (
    .addr(shifter_1_out), .we(Mem_write), .oe(Mem_Read), .clk(CLK));  // open: data
endmodule

module DataInstructions (
  input  [31:0] Address,
  input  CLK,
  output [31:0] out_3
);

  wire [23:0] shifter_1_out;

  Shifter #(.width(24), .shift("lr")) shifter_1 (.in(Address[23:0]), .\dist (5'b00010), .out(shifter_1_out));
  RAM #(.addrWidth(24), .dataWidth(32)) ram_1 (.addr(shifter_1_out), .oe(1'b1), .clk(CLK), .data(out_3));  // open: we
endmodule

module ALUCtrl (
  input  [1:0] ALUOp,
  input  [5:0] Funct,
  output [2:0] ALUOperation
);

  ALUCtrlCal aluctrlcal_1 (
    .OP1(ALUOp[1]), .OP0(ALUOp[0]), .F5(Funct[5]), .F4(Funct[4]), .F3(Funct[3]), .F2(Funct[2]),
    .F1(Funct[1]), .F0(Funct[0]), .ALU2(ALUOperation[2]), .ALU1(ALUOperation[1]), .ALU0(ALUOperation[0]));
endmodule

module Funct (
  input  funct1,
  input  funct2,
  input  funct3,
  input  funct4,
  output s1,
  output s2,
  output s3
);

  wire and_1_out, and_2_out, not_1_out, not_2_out, not_3_out;

  or or_1 (s1, funct4, funct1);
  not not_1 (not_1_out, funct2);
  and and_1 (and_1_out, not_1_out, not_2_out);
  not not_2 (not_2_out, funct3);
  not not_3 (not_3_out, funct3);
  and and_2 (and_2_out, not_3_out, funct4);
  not not_4 (s3, funct2);
  or or_2 (s2, and_1_out, and_2_out, funct1);

  // Notes on the sheet:
  //   SLT 111
  //   AND 000
  //   OR 110
  //   NOR100
  //   ADD 011
  //   RESTA 001
endmodule

module CalcOp (
  input  in_1,
  input  in_2,
  output out_3
);

  wire not_1_out;

  not not_1 (not_1_out, in_2);
  and and_1 (out_3, in_1, not_1_out);
endmodule

module ALUCtrlCal (
  input  OP1,
  input  OP0,
  input  F5,
  input  F4,
  input  F3,
  input  F2,
  input  F1,
  input  F0,
  output ALU2,
  output ALU1,
  output ALU0
);

  wire and_1_out, and_2_out, and_3_out, and_4_out, and_5_out, and_6_out, and_7_out, and_8_out, and_9_out,
       and_10_out, not_1_out, not_2_out, not_3_out, not_4_out, not_5_out, not_6_out, not_7_out, not_8_out,
       not_9_out, not_10_out, not_11_out;

  and and_1 (and_1_out, OP1, not_1_out, F0);
  not not_1 (not_1_out, F5);
  and and_2 (and_2_out, OP1, not_2_out, F0);
  not not_2 (not_2_out, F2);
  not not_3 (not_3_out, F1);
  and and_3 (and_3_out, OP1, not_3_out, F0);
  and and_4 (and_4_out, OP1, F4, F0);
  and and_5 (and_5_out, OP1, F5, F3);
  not not_4 (not_4_out, OP1);
  not not_5 (not_5_out, F2);
  and and_6 (and_6_out, not_5_out, not_6_out);
  not not_6 (not_6_out, F1);
  not not_7 (not_7_out, F3);
  and and_7 (and_7_out, not_7_out, F0);
  and and_8 (and_8_out, F3, not_8_out);
  not not_8 (not_8_out, F2);
  not not_9 (not_9_out, F2);
  not not_10 (not_10_out, F4);
  not not_11 (not_11_out, F3);
  or or_1 (ALU1, not_4_out, and_6_out, and_7_out, and_8_out);
  and and_9 (and_9_out, OP1, F5, not_9_out);
  and and_10 (and_10_out, OP1, F5, not_10_out, not_11_out, F1, F0);
  or or_2 (ALU2, OP0, and_1_out, and_2_out, and_3_out, and_4_out, and_5_out);
  or or_3 (ALU0, OP0, and_9_out, and_10_out);
endmodule
